# Fritzing sketch Tisch-komplett (saved by Fritzing 0.9.5d)

parts:
  U1 = Spannungsversorgung 230V [chip_label="Spannungsversorgung 230V" package="SIP (Single Inline) [THT]"]
  U4 = 24V Netzteil [chip_label="24V Netzteil" package="SIP (Single Inline) [THT]"]
  U3 = 12V Netzteil [chip_label="12V Netzteil" package="SIP (Single Inline) [THT]"]
  U5 = 5V Netzteil [chip_label="5V Netzteil" package="SIP (Single Inline) [THT]"]
  M1 = 1 chan 5v relay module
  U6 = 5V Netzteil [chip_label="5V Netzteil" package="SIP (Single Inline) [THT]"]
  J1 = Wago 221-413
  J2 = Wago 221-413
  U7 = Spannungsversorgung 230V [chip_label="Spannungsversorgung 230V" package="SIP (Single Inline) [THT]"]  # not connected
  U8 = Spannungsversorgung 230V [chip_label="Spannungsversorgung 230V" package="SIP (Single Inline) [THT]"]
  U13 = Spannungsversorgung 230V [chip_label="Spannungsversorgung 230V" package="SIP (Single Inline) [THT]"]
  U14 = Spannungsversorgung 230V [chip_label="Spannungsversorgung 230V" package="SIP (Single Inline) [THT]"]  # not connected
  IC1 = IC, SIP package, 5 pins [chip_label=MFC]  # not connected
  U15 = Ventil 12V - alt [chip_label="2-Pin Stecker" package="SIP (Single Inline) [THT]"]  # not connected
  U9 = Ventil 12V - alt [chip_label="2-Pin Stecker" package="SIP (Single Inline) [THT]"]  # not connected
  U18 = Ventil 12V - alt [chip_label="2-Pin Stecker" package="SIP (Single Inline) [THT]"]  # not connected
  U10 = Ventil 12V - alt [chip_label="2-Pin Stecker" package="SIP (Single Inline) [THT]"]  # not connected
  U17 = Ventil 12V - alt [chip_label="2-Pin Stecker" package="SIP (Single Inline) [THT]"]  # not connected
  U16 = Ventil 12V - alt [chip_label="2-Pin Stecker" package="SIP (Single Inline) [THT]"]  # not connected
  U12 = Ventil 12V - alt [chip_label="2-Pin Stecker" package="SIP (Single Inline) [THT]"]  # not connected
  U11 = Ventil 12V - alt [chip_label="2-Pin Stecker" package="SIP (Single Inline) [THT]"]  # not connected
  U19 = Ventil 12V - alt [chip_label="2-Pin Stecker" package="SIP (Single Inline) [THT]"]  # not connected
  U20 = Ventil 12V - alt [chip_label="2-Pin Stecker" package="SIP (Single Inline) [THT]"]  # not connected
  U21 = Ventil 12V [chip_label="Ventil 12V" package="SIP (Single Inline) [THT]"]  # not connected
  J3 = Wago 221-413
  J5 = Wago 221-413
  J6 = Wago 221-413
  IC2 = IC, DIP package, 6 pins [chip_label=Windrad-Connector]
  IC3 = IC, SIP package, 3 pins [chip_label=Windrad]
  IC4 = IC, DIP package, 6 pins [chip_label=Windrad-Connector]
  IC5 = IC, SIP package, 3 pins [chip_label=Windrad]
  U22 = ESP32S-HiLetgo [part_number=ESP32S-HiLetgo]  # not connected
  A1 = Raspberry Pi 5  # not connected
  U23 = Module 4 Relais 5V [package="Module 4 Relais 5V"]  # not connected
  U24 = 12V Netzteil [chip_label="12V Netzteil" package="SIP (Single Inline) [THT]"]  # not connected
  Kühler = SIP - 2 pins [chip_label=Kühler package="SIP (Single Inline) [THT]"]  # not connected
  Heizstab = 230V Spannungsabnehmer [chip_label=230V-Spannungsabnehmer package="SIP (Single Inline) [THT]"]  # not connected
  U25 = ESP32S-HiLetgo [part_number=ESP32S-HiLetgo]  # not connected
  Pumpe = IC, SIP package, 5 pins [chip_label=230V-Spannungsabnehmer]  # not connected

nets:
  N1: U1.Phase, M1.pin_5, U6.Phase
  N2: U1.Neutral, U6.Neutral, J2.Pin_1, J2.Pin_3
  N3: U1.Schutz, U6.Schutz
  N4: U4.Phase, U3.Phase, U5.Phase
  N5: U4.Neutral, U3.Neutral, U5.Neutral
  N6: U4.Schutz, U3.Schutz, U5.Schutz
  N7: M1.pin_4, J1.Pin_1
  N8: U8.Phase, U13.Phase, J3.Pin_1, J3.Pin_3
  N9: U8.Neutral, U13.Neutral, J5.Pin_1, J5.Pin_3
  N10: U8.Schutz, U13.Schutz, J6.Pin_1, J6.Pin_3
  N11: IC2.pin4, IC3.pin3
  N12: IC2.pin5, IC3.pin2
  N13: IC2.pin6, IC3.pin1
  N14: IC4.pin4, IC5.pin3
  N15: IC4.pin5, IC5.pin2
  N16: IC4.pin6, IC5.pin1

custom parts:
  Spannungsversorgung 230V: A SIP stand-in part for whatever you want. With 3 pins on a 300 mil single inline package (SIP) footprint.
  24V Netzteil: A SIP stand-in part for whatever you want. With 5 pins on a 300 mil single inline package (SIP) footprint.
  12V Netzteil: A SIP stand-in part for whatever you want. With 5 pins on a 300 mil single inline package (SIP) footprint.
  5V Netzteil: A SIP stand-in part for whatever you want. With 5 pins on a 300 mil single inline package (SIP) footprint.
  1 chan 5v relay module: 1 Channel 5V Relay Module Board Shield with Optocoupler Support High and Low Level Trigger for Arduino.
  Wago 221-413: Wago 221-413 3 position splicing connector 12AWG.
  Ventil 12V - alt: A SIP stand-in part for whatever you want. With 2 pins on a 300 mil single inline package (SIP) footprint.
  Ventil 12V: A SIP stand-in part for whatever you want. With 3 pins on a 300 mil single inline package (SIP) footprint.
  ESP32S-HiLetgo: HiLetgo ESP-WROOM-32 ESP32 ESP-32S Development Board 2.4GHz Dual-Mode WiFi + Bluetooth Dual Cores Microcontroller The ESP32 integrated with Antenna switches, RF Balun, power amplifiers, low-noise amplifiers, filters, and management modules, and the entire solution occupies the least area of PCB. 2.4 GHz Wi-Fi plus Bluetooth dual-mode chip, with TSMC Ultra-low power consumption 40nm technology,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
  Raspberry Pi 5: The RPi5, a faster version of the awesome Raspberry Pi4B ARM Board with 40 pin gpio.
  Module 4 Relais 5V: Module 4 Relais 5V 4x SPD-06VDC-SD-C
  230V Spannungsabnehmer: A SIP stand-in part for whatever you want. With 3 pins on a 300 mil single inline package (SIP) footprint.
